# Fritzing sketch Elektronik (saved by Fritzing 0.9.3b)
breadboards: 1

parts:
  R1 = Resistor [tolerance=±5% resistance=100k package=THT]
  LED1 = LED - 5mm [color="White (8000K)" package="5 mm [THT]"]
  Q1 = LTR-301 [package=ltr-301]
  IR_Empfänger_für_Fernbedienung = TSOP312.., 314.. [package=THT]
  D1 = LTE-302 [package=lte-302]
  Raspberry_Pi1 = Raspberry Pi 2
  R2 = Resistor [tolerance=±5% resistance=470 package=THT]
  S1 = Momentary Switch [package=ksa_sealed_tac_switch]
  S2 = Momentary Switch [package=ksa_sealed_tac_switch]
  S3 = Momentary Switch [package=ksa_sealed_tac_switch]
  R3 = Resistor [tolerance=±5% resistance=470 package=THT]

nets:
  N1: R1.Pin_0, IR_Empfänger_für_Fernbedienung.Vs, Raspberry_Pi1.3v3, R3.Pin_0
  N2: R1.Pin_1, D1.A, R2.Pin_0
  GND: LED1.cathode, Q1.C, IR_Empfänger_für_Fernbedienung.GND, D1.C, Raspberry_Pi1.GND, S1.1, S1.2, S2.1, S2.2, S3.1, S3.2
  N3: LED1.anode, Raspberry_Pi1.GPIO17
  N4: Q1.E, R3.Pin_1
  N5: IR_Empfänger_für_Fernbedienung.Data, Raspberry_Pi1.GPIO23
  N6: Raspberry_Pi1.GPIO4, R2.Pin_1
  N7: Raspberry_Pi1.GPIO18, S3.3, S3.4
  N8: Raspberry_Pi1.GPIO15, S2.3, S2.4
  N9: Raspberry_Pi1.GPIO14, S1.3, S1.4

notes:
  Die Empfänger der Lichtschranke (schwarz) ist mit PIN 4 verbunden, die LED mit PIN 17.
  Die Schalter liegen auf den PINS 14, 15 und 18.
  Der Daten-PIN des IR-Empfängers liegt auf PIN 23.
